# Fritzing sketch deluxe_diagram (saved by Fritzing 0.8.3b)
breadboards: 1

parts:
  Part1 = Arduino Uno (Rev3)
  J1 = female pin header, 4 pins [form="♀ (female)"]
  J2 = female pin header, 4 pins [form="♀ (female)"]
  J3 = female pin header, 4 pins [form="♀ (female)"]
  J4 = female pin header, 4 pins [form="♀ (female)"]
  J5 = male pin header, 4 pins [form="♂ (male)"]

nets:
  N1: Part1.ICSP_MISO, Part1.D12/MISO, J1.pin2, J3.pin2
  N2: Part1.ICSP_MOSI, Part1.D11_PWM/MOSI, J1.pin3, J3.pin3
  N3: Part1.GND, J1.pin1, J2.pin1, J3.pin1, J4.pin1, J5.pin3
  N4: Part1.D0/RX, J5.pin2
  N5: Part1.D1/TX, J5.pin1
  N6: Part1.D6_PWM, J2.pin3, J4.pin3
  N7: Part1.D7, J2.pin2, J4.pin2
  N8: Part1.ioref, J1.pin4, J2.pin4, J3.pin4, J4.pin4, J5.pin4

notes:
  VCC
  Trig
  Echo
  GND
  gnd
  hc06
  vcc
  tx
  rx
