# Fritzing sketch 3vSupply (saved by Fritzing 0.9.2b)
breadboards: 1

parts:
  LED1 = LED - 5mm [color="Red (633nm)" package="5 mm [THT]"]
  R1 = Resistor [tolerance=±5% resistance=100 package=THT]
  C1 = Electrolytic Capacitor [capacitance=1µF package="100 mil [THT, electrolytic]"]
  IC2 = Voltage Regulator [package=to-92]
  J1 = female pin header, 2 pins [form="♀ (female)"]

nets:
  N1: LED1.cathode, R1.Pin_0
  N2: LED1.anode, C1.+, IC2.GND, J1.pin2
  N3: R1.Pin_1, C1.-, IC2.OUT
  N4: IC2.IN, J1.pin1

notes:
  3.3v Rail
  Ground

custom parts:
  Voltage Regulator: Voltage Regulator Standard TSC259033 3.3v regulator. IGO (Input Ground OUTPUT).
