# Fritzing sketch bare-basics (saved by Fritzing 0.9.6b)

parts:
  Mod1 = Raspberry Pi Pico
  IC1 = IC, DIP package, 40 pins [chip_label=WirelessPack]
  Mod2 = Raspberry Pi Pico
  IC2 = IC, DIP package, 40 pins [chip_label=WirelessPack]
  Mod3 = Raspberry Pi Pico  # not connected

nets:
  N1: Mod1.pin_10, IC1.pin10
  N2: Mod1.pin_14, IC1.pin14
  N3: Mod1.pin_15, IC1.pin15
  N4: Mod1.pin_21, IC1.pin21
  N5: Mod1.pin_23, Mod1.pin_42, IC1.pin23
  N6: Mod1.pin_24, IC1.pin24
  N7: Mod1.pin_25, IC1.pin25
  N8: Mod1.pin_36, IC1.pin36
  N9: Mod2.pin_14, IC2.pin14
  N10: Mod2.pin_15, IC2.pin15
  N11: Mod2.pin_21, IC2.pin21
  N12: Mod2.pin_23, Mod2.pin_42, IC2.pin23
  N13: Mod2.pin_24, IC2.pin24
  N14: Mod2.pin_25, IC2.pin25
  N15: Mod2.pin_31, IC2.pin10
  N16: Mod2.pin_36, IC2.pin36

notes:
  3v3
  miso
  mosi
  gnd
  sclk
  _reset
  busy
  _esp_cs
  Motor Board
  Original

custom parts:
  Raspberry Pi Pico: Raspberry Pi Pico. Based around the RP2040 microcontroller the Pico is a low cost microcontroller device bringing Raspberry Pi quality, cost, and easy of use to the microcontroller space. Jan 2021, Split part in to two versions: tht (this one) and SMD. This one will drill holes for a .1 in header in pcb to allow plugging in the module as well as providing pads to solder the module to the top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
